// Logisim project Encoder.circ as structural Verilog: 1 circuit, main circuit main
module main (
  input  Y7,
  input  Y6,
  input  Y5,
  input  Y4,
  input  Y3,
  input  Y2,
  input  Y1,
  output A0,
  output A1,
  output A2
);

  or or_1 (A0, Y7, Y6, Y4, Y5);
  or or_2 (A1, Y7, Y6, Y3, Y2);
  or or_3 (A2, Y7, Y5, Y4, Y1);

  // Notes on the sheet:
  //   Encoder
endmodule
