// Logisim project decoder.circ as structural Verilog: 1 circuit, main circuit main
module main (
  input  in_1,
  input  in_2,
  input  in_3
);

  // NOT_Gate not_1 has open pins: in=in_1, out=open
  // NOT_Gate not_2 has open pins: in=in_2, out=open
  // NOT_Gate not_3 has open pins: in=in_3, out=open
  // AND_Gate and_1 is placed but not wired
  // AND_Gate and_2 is placed but not wired
  // AND_Gate and_3 is placed but not wired
  // AND_Gate and_4 is placed but not wired
  // AND_Gate and_5 is placed but not wired
  // AND_Gate and_6 is placed but not wired
  // AND_Gate and_7 is placed but not wired
  // AND_Gate and_8 is placed but not wired
endmodule
