// Logisim project evenparity.circ as structural Verilog: 1 circuit, main circuit main
module main (
  input  X,
  input  Y,
  input  Z,
  input  X_2,
  input  Y_2,
  input  Z_2,
  input  P,
  output Parity,
  output out_9
);

  wire xor_1_out, xor_2_out, xor_3_out;

  xor xor_1 (xor_1_out, X, Y);
  xor xor_2 (xor_2_out, X_2, Y_2);
  xor xor_3 (xor_3_out, Z_2, P);
  xor xor_4 (Parity, xor_1_out, Z);
  xor xor_5 (out_9, xor_2_out, xor_3_out);

  // Notes on the sheet:
  //   Parity chceker
  //   Parity Genrator
  //   Even Parity Generator and checker
endmodule
