// Logisim project oddparity.circ as structural Verilog: 1 circuit, main circuit main
module main (
  input  X,
  input  Y,
  input  Z,
  input  X_2,
  input  Y_2,
  input  Z_2,
  input  P,
  output out_8,
  output out_9
);

  wire xnor_1_out, xnor_2_out, xnor_3_out;

  xnor xnor_1 (xnor_1_out, X, Y);
  xnor xnor_2 (xnor_2_out, X_2, Y_2);
  xor xor_1 (out_8, xnor_1_out, Z);
  xnor xnor_3 (xnor_3_out, Z_2, P);
  xnor xnor_4 (out_9, xnor_2_out, xnor_3_out);

  // Notes on the sheet:
  //   Parity chceker
  //   Parity Genrator
  //   odd Parity generator and checker
endmodule
